// Logisim project CPU.circ as structural Verilog: 7 circuits, main circuit main
module MyALU (
  input  Cin,
  input  M,
  input  [3:0] Op,
  input  [3:0] A,
  input  [3:0] B,
  output [3:0] Out,
  output A_B,
  output Sign
);

  wire dip_74181_1_p1, dip_74181_1_p2, dip_74181_1_p3, dip_74181_1_p10, dip_74181_1_p11, dip_74181_1_p12,
       dip_74181_1_p13, dip_74181_1_p14, dip_74181_1_p15, dip_74181_1_p16, dip_74181_1_p17, dip_74181_1_p18,
       dip_74181_1_p19, dip_74181_1_p20, dip_74181_1_p23, not_5_out;

  not not_1 (Out[0], dip_74181_1_p10);
  not not_2 (Out[2], dip_74181_1_p12);
  not not_3 (Out[3], dip_74181_1_p23);
  not not_4 (Out[1], dip_74181_1_p11);
  // DIP_74181 dip_74181_1: pin names not known; wires that end beside it: dip_74181_1_p1, dip_74181_1_p2, dip_74181_1_p3, Op[0], Op[1], Op[2], Op[3], Cin, M, dip_74181_1_p10, dip_74181_1_p11, dip_74181_1_p12, dip_74181_1_p13, dip_74181_1_p14, dip_74181_1_p15, dip_74181_1_p16, dip_74181_1_p17, dip_74181_1_p18, dip_74181_1_p19, dip_74181_1_p20, dip_74181_1_p1, A_B, dip_74181_1_p23, dip_74181_1_p20
  not not_5 (not_5_out, A_B);
  and and_1 (Sign, not_5_out, dip_74181_1_p19);
  not not_6 (dip_74181_1_p3, A[0]);
  not not_7 (dip_74181_1_p13, A[1]);
  not not_8 (dip_74181_1_p15, A[2]);
  not not_9 (dip_74181_1_p17, A[3]);
  not not_10 (dip_74181_1_p2, B[0]);
  not not_11 (dip_74181_1_p14, B[1]);
  not not_12 (dip_74181_1_p16, B[2]);
  not not_13 (dip_74181_1_p18, B[3]);

  // Notes on the sheet:
  //   G
  //   Cout
  //   M
endmodule

module MyTrigger (
  input  Clock,
  input  [3:0] D,
  output [3:0] Q
);

  D_Flip_Flop d_ff_1 (.clk(Clock), .D(D[0]), .Q(Q[0]), .en(1'b1));  // open: Qn, preset, reset
  D_Flip_Flop d_ff_2 (.clk(Clock), .D(D[1]), .Q(Q[1]), .en(1'b1));  // open: Qn, preset, reset
  D_Flip_Flop d_ff_3 (.clk(Clock), .D(D[2]), .Q(Q[2]), .en(1'b1));  // open: Qn, preset, reset
  D_Flip_Flop d_ff_4 (.clk(Clock), .D(D[3]), .Q(Q[3]), .en(1'b1));  // open: Qn, preset, reset
endmodule

module Registers (
  input  w,
  input  [3:0] data,
  input  [3:0] A,
  input  [3:0] B,
  input  [3:0] to,
  output [3:0] A_2,
  output [3:0] r0,
  output [3:0] r1,
  output [3:0] r2,
  output [3:0] B_2,
  output [3:0] r3,
  output [3:0] r4,
  output [3:0] r4_2,
  output [3:0] r4_3,
  output [3:0] r4_4
);

  wire r0_w, r1_w, r2_w, r3_w, r4_w, r5_w, r6_w, r7_w;

  Demultiplexer #(.select(3), .enable("false")) demultiplexer_1 (
    .out0(r0_w), .out1(r1_w), .out2(r2_w), .out3(r3_w), .out4(r4_w), .out5(r5_w), .out6(r6_w), .out7(r7_w),
    .in(w), .sel(to[2:0]));
  MyTrigger mytrigger_1 (.D(data), .Clock(r0_w), .Q(r0));
  MyTrigger mytrigger_2 (.D(data), .Clock(r1_w), .Q(r1));
  MyTrigger mytrigger_3 (.D(data), .Clock(r2_w), .Q(r2));
  MyTrigger mytrigger_4 (.D(data), .Clock(r3_w), .Q(r3));
  MyTrigger mytrigger_5 (.D(data), .Clock(r4_w), .Q(r4));
  MyTrigger mytrigger_6 (.D(data), .Clock(r5_w), .Q(r4_2));
  MyTrigger mytrigger_7 (.D(data), .Clock(r6_w), .Q(r4_3));
  MyTrigger mytrigger_8 (.D(data), .Clock(r7_w), .Q(r4_4));
  Multiplexer #(.select(3), .width(4), .enable("false")) multiplexer_1 (
    .in0(r0), .in1(r1), .in2(r2), .in3(r3), .in4(r4), .in5(r4_2), .in6(r4_3), .in7(r4_4), .out(A_2),
    .sel(A[2:0]));
  Multiplexer #(.select(3), .width(4), .enable("false")) multiplexer_2 (
    .in0(r0), .in1(r1), .in2(r2), .in3(r3), .in4(r4), .in5(r4_2), .in6(r4_3), .in7(r4_4), .out(B_2),
    .sel(B[2:0]));

  // Other names for the same wires on the sheet: r5[3:0] = r4_2; r6[3:0] = r4_3; r7[3:0] = r4_4
endmodule

module main (
  output [3:0] out_1,
  output [3:0] out_2,
  output [3:0] out_3,
  output [3:0] out_4,
  output [3:0] out_5,
  output [3:0] out_6,
  output [3:0] out_7,
  output [3:0] out_8,
  output [3:0] out_9,
  output [3:0] out_10,
  output [3:0] out_11,
  output [3:0] out_12,
  output [3:0] out_13,
  output [3:0] out_14,
  output [3:0] out_15,
  output [1:0] out_16
);

  wire address, Alu, and_1_out, and_2_out, cin, clock_1_out, D, demultiplexer_1_out1, DoJmp, f, Jump, M,
       not_1_out, not_2_out, not_3_out, or_1_out, w, Write;
  wire [1:0] myalu_1_sign;
  wire [3:0] multiplexer_1_out, Op, pc_1_command, RD;

  not not_1 (not_1_out, D);
  Demultiplexer #(.enable("false")) demultiplexer_1 (
    .out0(w), .out1(demultiplexer_1_out1), .in(Write), .sel(and_1_out));
  Multiplexer #(.width(4), .enable("false")) multiplexer_1 (
    .in0(out_11), .in1(out_1), .out(multiplexer_1_out), .sel(not_1_out));
  and and_1 (and_1_out, address, D);
  Multiplexer #(.select(2), .width(4), .enable("false")) multiplexer_2 (
    .in0(out_1), .in1(out_13), .in2(RD), .in3(out_1), .out(out_6), .sel({address, D}));
  RAM #(.addrWidth(4), .dataWidth(4), .bus("separate")) ram_1 (
    .addr(multiplexer_1_out), .din(out_14), .data(RD), .str(demultiplexer_1_out1),
    .clk(demultiplexer_1_out1), .ld(1'b1));  // open: sel, clr
  Multiplexer #(.width(4), .enable("false")) multiplexer_3 (.in0(out_6), .in1(out_15), .out(out_14), .sel(Alu));
  Registers registers_1 (
    .A(out_12), .B(out_13), .r0(out_2), .r1(out_4), .r2(out_7), .r3(out_9), .data(out_14), .w(w),
    .to(out_12), .r4(out_3), .B_2(out_1), .A_2(out_11), .r4_2(out_5), .r4_3(out_8), .r4_4(out_10));
  MyALU myalu_1 (
    .Op(Op), .Out(out_15), .M(M), .A(out_11), .B(out_6), .A_B(myalu_1_sign[1]), .Cin(cin),
    .Sign(myalu_1_sign[0]));
  _2_bit_Trigger u_2_bit_trigger_1 (.Clock(and_2_out), .D(myalu_1_sign), .Q(out_16));
  and and_2 (and_2_out, f, not_2_out);
  not not_2 (not_2_out, clock_1_out);
  Clock clock_1 (.out(clock_1_out));
  or or_1 (or_1_out, out_16[1], out_16[0]);
  not not_3 (not_3_out, out_16[0]);
  PC pc_1 (
    .Clock(clock_1_out), .B(out_13), .A(out_12), .command(pc_1_command), .DoJump(DoJmp), .Clock_2(clock_1_out));  // open: out_9, out_8, in_3
  Multiplexer #(.select(2), .enable("false")) multiplexer_4 (
    .in0(out_16[0]), .in1(out_16[1]), .in2(or_1_out), .in3(not_3_out), .out(DoJmp), .sel(Op[1:0]));
  Decode_Logic decode_logic_1 (
    .Jump(Jump), .AluLogic(M), .Alu(Alu), .Bit(1'b1), .AluCarry(cin), .FWright(f), .Address(address),
    .AluOp(Op), .Op(pc_1_command), .Digit(D));
  nor nor_1 (Write, clock_1_out, Jump);

  // Other names for the same wires on the sheet: A[3:0] = out_11; A_in[3:0] = out_12; AluOut[3:0] = out_15;
  //   B[3:0] = out_1; B_in[3:0] = out_13; data[3:0] = out_14; ID[3:0] = out_6; r0[3:0] = out_2; r1[3:0] = out_4;
  //   r2[3:0] = out_7; r3[3:0] = out_9; r4[3:0] = out_3; r5[3:0] = out_5; r6[3:0] = out_8; r7[3:0] = out_10
endmodule

module _2_bit_Trigger (
  input  Clock,
  input  [1:0] D,
  output [1:0] Q
);

  D_Flip_Flop d_ff_1 (.clk(Clock), .D(D[0]), .Q(Q[1]), .en(1'b1));  // open: Qn, preset, reset
  D_Flip_Flop d_ff_2 (.clk(Clock), .D(D[1]), .Q(Q[0]), .en(1'b1));  // open: Qn, preset, reset
endmodule

module Decode_Logic (
  input  Bit,
  input  [3:0] Op,
  output Digit,
  output Jump,
  output AluLogic,
  output Alu,
  output AluCarry,
  output FWright,
  output Address,
  output [3:0] AluOp
);

  wire demultiplexer_1_out1, demultiplexer_1_out2, demultiplexer_1_out3, demultiplexer_1_out9;

  Demultiplexer #(.select(4), .enable("false")) demultiplexer_1 (
    .out1(demultiplexer_1_out1), .out2(demultiplexer_1_out2), .out3(demultiplexer_1_out3), .out4(AluLogic),
    .out6(AluCarry), .out9(demultiplexer_1_out9), .in(Bit), .sel(Op));  // open: out0, out5, out7, out8, out10, out11, out12, out13, out14, out15
  and and_1 (Jump, Op[2], Op[3]);
  or or_1 (Digit, demultiplexer_1_out2, demultiplexer_1_out1);
  or or_2 (Address, demultiplexer_1_out2, demultiplexer_1_out3);
  or or_3 (Alu, AluLogic, AluCarry, demultiplexer_1_out9);

  assign AluOp = Op;
  assign FWright = AluCarry;

  // Other names for the same wires on the sheet: adress = Address; FlagWright = AluCarry
endmodule

module PC (
  input  Clock,
  input  DoJump,
  input  in_3,
  input  Clock_2,
  output [3:0] B,
  output [3:0] A,
  output [3:0] command,
  output [3:0] out_8,
  output [3:0] out_9
);

  wire and_1_out, and_2_out, not_1_out, not_2_out;
  wire [7:0] counter_1_q;

  and and_1 (and_1_out, command[3], command[2], DoJump);
  not not_1 (not_1_out, and_1_out);
  Counter counter_1 (
    .load(and_1_out), .D({A, B}), .count(not_1_out), .Q(counter_1_q), .clk(Clock));  // open: carry, clr
  Counter #(.width(4), .max('hf)) counter_2 (.count(in_3), .Q(out_8), .clk(not_2_out));  // open: load, D, carry, clr
  Counter #(.width(4), .max('hf)) counter_3 (.count(in_3), .Q(out_9), .clk(Clock_2));  // open: load, D, carry, clr
  ROM #(.dataWidth(12)) rom_1 (.addr(counter_1_q), .data({command, A, B}), .sel(1'b1));
  not not_2 (not_2_out, and_2_out);
  and and_2 (and_2_out, out_9[0], out_9[1], out_9[2], out_9[3]);

  // Other names for the same wires on the sheet: Address[7:0] = {A, B}

  // Notes on the sheet:
  //   contents of rom_1 (hex, n*v repeats v):
  //   0 121 100 116 201 113 902 201 902 110 201 114 902 201 115 902 201 112 902 201 111 902 201 137 101 60
  //   663 c30 340 10 612 d29 371 674 e29 51 952 361 256 666 c1e 61 962 264 902 677 c19
endmodule
