// Logisim project CPU.circ as structural Verilog: 11 circuits, main circuit main
module MyALU (
  input  Cin,
  input  M,
  input  [3:0] Op,
  input  [3:0] A,
  input  [3:0] B,
  output [3:0] Out,
  output A_B,
  output Sign
);

  wire dip_74181_1_p1, dip_74181_1_p2, dip_74181_1_p3, dip_74181_1_p10, dip_74181_1_p11, dip_74181_1_p12,
       dip_74181_1_p13, dip_74181_1_p14, dip_74181_1_p15, dip_74181_1_p16, dip_74181_1_p17, dip_74181_1_p18,
       dip_74181_1_p19, dip_74181_1_p20, dip_74181_1_p23, not_5_out;

  not not_1 (Out[0], dip_74181_1_p10);
  not not_2 (Out[2], dip_74181_1_p12);
  not not_3 (Out[3], dip_74181_1_p23);
  not not_4 (Out[1], dip_74181_1_p11);
  // DIP_74181 dip_74181_1: pin names not known; wires that end beside it: dip_74181_1_p1, dip_74181_1_p2, dip_74181_1_p3, Op[0], Op[1], Op[2], Op[3], Cin, M, dip_74181_1_p10, dip_74181_1_p11, dip_74181_1_p12, dip_74181_1_p13, dip_74181_1_p14, dip_74181_1_p15, dip_74181_1_p16, dip_74181_1_p17, dip_74181_1_p18, dip_74181_1_p19, dip_74181_1_p20, dip_74181_1_p1, A_B, dip_74181_1_p23, dip_74181_1_p20
  not not_5 (not_5_out, A_B);
  and and_1 (Sign, not_5_out, dip_74181_1_p19);
  not not_6 (dip_74181_1_p3, A[0]);
  not not_7 (dip_74181_1_p13, A[1]);
  not not_8 (dip_74181_1_p15, A[2]);
  not not_9 (dip_74181_1_p17, A[3]);
  not not_10 (dip_74181_1_p2, B[0]);
  not not_11 (dip_74181_1_p14, B[1]);
  not not_12 (dip_74181_1_p16, B[2]);
  not not_13 (dip_74181_1_p18, B[3]);

  // Notes on the sheet:
  //   G
  //   Cout
  //   M
endmodule

module MyTrigger (
  input  Clock,
  input  [3:0] D,
  output [3:0] Q
);

  D_Flip_Flop d_ff_1 (.clk(Clock), .D(D[0]), .Q(Q[0]), .en(1'b1));  // open: Qn, preset, reset
  D_Flip_Flop d_ff_2 (.clk(Clock), .D(D[1]), .Q(Q[1]), .en(1'b1));  // open: Qn, preset, reset
  D_Flip_Flop d_ff_3 (.clk(Clock), .D(D[2]), .Q(Q[2]), .en(1'b1));  // open: Qn, preset, reset
  D_Flip_Flop d_ff_4 (.clk(Clock), .D(D[3]), .Q(Q[3]), .en(1'b1));  // open: Qn, preset, reset
endmodule

module Registers (
  input  w,
  input  [3:0] data,
  input  [3:0] A,
  input  [3:0] B,
  input  [3:0] to,
  output [3:0] A_2,
  output [3:0] r0,
  output [3:0] B_2,
  output [3:0] r1,
  output [3:0] r2,
  output [3:0] r3,
  output [3:0] r4,
  output [3:0] r4_2,
  output [3:0] r4_3,
  output [3:0] r4_4
);

  wire r0_w, r1_w, r2_w, r3_w, r4_w, r5_w, r6_w, r7_w;

  Demultiplexer #(.select(3), .enable("false")) demultiplexer_1 (
    .out0(r0_w), .out1(r1_w), .out2(r2_w), .out3(r3_w), .out4(r4_w), .out5(r5_w), .out6(r6_w), .out7(r7_w),
    .in(w), .sel(to[2:0]));
  MyTrigger mytrigger_1 (.D(data), .Clock(r0_w), .Q(r0));
  MyTrigger mytrigger_2 (.D(data), .Clock(r1_w), .Q(r1));
  MyTrigger mytrigger_3 (.D(data), .Clock(r2_w), .Q(r2));
  MyTrigger mytrigger_4 (.D(data), .Clock(r3_w), .Q(r3));
  MyTrigger mytrigger_5 (.D(data), .Clock(r4_w), .Q(r4));
  MyTrigger mytrigger_6 (.D(data), .Clock(r5_w), .Q(r4_2));
  MyTrigger mytrigger_7 (.D(data), .Clock(r6_w), .Q(r4_3));
  MyTrigger mytrigger_8 (.D(data), .Clock(r7_w), .Q(r4_4));
  Multiplexer #(.select(3), .width(4), .enable("false")) multiplexer_1 (
    .in0(r0), .in1(r1), .in2(r2), .in3(r3), .in4(r4), .in5(r4_2), .in6(r4_3), .in7(r4_4), .out(A_2),
    .sel(A[2:0]));
  Multiplexer #(.select(3), .width(4), .enable("false")) multiplexer_2 (
    .in0(r0), .in1(r1), .in2(r2), .in3(r3), .in4(r4), .in5(r4_2), .in6(r4_3), .in7(r4_4), .out(B_2),
    .sel(B[2:0]));

  // Other names for the same wires on the sheet: r5[3:0] = r4_2; r6[3:0] = r4_3; r7[3:0] = r4_4
endmodule

module main (
  output [3:0] out_1,
  output [3:0] out_2,
  output [3:0] out_3,
  output [3:0] out_4,
  output [3:0] out_5,
  output [3:0] out_6,
  output [3:0] out_7,
  output [3:0] out_8,
  output [3:0] out_9,
  output [3:0] out_10,
  output [3:0] out_11,
  output [3:0] out_12,
  output [3:0] out_13,
  output [3:0] out_14,
  output [7:0] out_15
);

  wire _0, _0_out, _1_out, address, Alu, and_1_out, and_2_out, and_3_out, cin, clk, D, demultiplexer_1_out1,
       DoJmp, f, IRQ, IRQDone, Jump, M, not_1_out, not_2_out, not_3_out, not_4_out, or_1_out, or_2_out,
       rClkMv, SVCmd, SvEnd, SVSel, w, Write;
  wire [1:0] myalu_1_sign, n2_bit_trigger_1_q;
  wire [3:0] AluOut, IRC, multiplexer_1_out, multiplexer_4_out, multiplexer_5_out, Op, PCop, RD;
  wire [7:0] ircdecoder_1_ihaddr, SvAddrs, svdecoder_1_svbeg, svdecoder_1_svlen;

  not not_1 (not_1_out, D);
  Multiplexer #(.width(4), .enable("false")) multiplexer_1 (
    .in0(out_11), .in1(out_12), .out(multiplexer_1_out), .sel(not_1_out));
  Demultiplexer #(.enable("false")) demultiplexer_1 (
    .out0(w), .out1(demultiplexer_1_out1), .in(Write), .sel(and_1_out));
  and and_1 (and_1_out, D, address);
  LED led_1 (.in(out_10[0]));
  Multiplexer #(.width(4), .enable("false")) multiplexer_2 (.in0(out_6), .in1(AluOut), .out(out_3), .sel(Alu));
  TTY #(.rows(5), .cols(33)) tty_1 (.data({out_4[2:0], out_7}), .clk(out_4[3]), .we(1'b1));  // open: clr
  Multiplexer #(.select(2), .width(4), .enable("false")) multiplexer_3 (
    .in0(out_12), .in1(out_14), .in2(RD), .in3(out_12), .out(out_6), .sel({address, D}));
  RAM #(.addrWidth(4), .dataWidth(4), .bus("separate")) ram_1 (
    .addr(multiplexer_1_out), .din(out_3), .data(RD), .str(demultiplexer_1_out1), .clk(demultiplexer_1_out1),
    .ld(1'b1));  // open: sel, clr
  BinKeyboard binkeyboard_1 (.Key0(_0_out), .Rec(IRQDone), .Key1(_1_out), .IRQ(IRQ), .IRC(IRC));
  Button u__0 (.out(_0_out));
  Button _1 (.out(_1_out));
  Decode_Logic decode_logic_1 (
    .Jump(Jump), .AluLogic(M), .Alu(Alu), .Bit(1'b1), .AluCarry(cin), .FWright(f), .Address(address),
    .AluOp(Op), .Digit(D), .SVR_Command(SVCmd), .Op(PCop), .SVR_Select(SVSel), .rClkMv(rClkMv));
  Multiplexer #(.width(4), .enable("false")) multiplexer_4 (
    .in0(out_15[3:0]), .in1(out_15[7:4]), .out(multiplexer_4_out), .sel(out_14[0]));
  Registers registers_1 (
    .A(out_13), .B(out_14), .r0(out_1), .r1(out_4), .r2(out_7), .r3(out_9), .data(multiplexer_5_out), .w(w),
    .to(out_13), .r4(out_2), .B_2(out_12), .A_2(out_11), .r4_2(out_5), .r4_3(out_8), .r4_4(out_10));
  Multiplexer #(.width(4), .enable("false")) multiplexer_5 (
    .in0(out_3), .in1(multiplexer_4_out), .out(multiplexer_5_out), .sel(rClkMv));
  MyALU myalu_1 (
    .Op(Op), .Out(AluOut), .M(M), .A(out_11), .B(out_6), .A_B(myalu_1_sign[1]), .Cin(cin),
    .Sign(myalu_1_sign[0]));
  SVDecoder svdecoder_1 (.SVBeg(svdecoder_1_svbeg), .SVLen(svdecoder_1_svlen), .B(out_14), .Clk(SVSel));
  _2_bit_Trigger u_2_bit_trigger_1 (.Clock(and_2_out), .D(myalu_1_sign), .Q(n2_bit_trigger_1_q));
  or or_1 (or_1_out, ~SvEnd, SVCmd);  // OR_Gate
  and and_2 (and_2_out, f, not_2_out);
  not not_2 (not_2_out, clk);
  Clock clock_1 (.out(clk));
  and and_3 (and_3_out, or_1_out, clk);
  severalizer severalizer_1 (
    .SvBeg(svdecoder_1_svbeg), .CmdAddrs(SvAddrs), .End(SvEnd), .SvLen(svdecoder_1_svlen), .Clk(and_3_out));
  or or_2 (or_2_out, n2_bit_trigger_1_q[1], n2_bit_trigger_1_q[0]);
  Multiplexer #(.select(2), .enable("false")) multiplexer_6 (
    .in0(n2_bit_trigger_1_q[0]), .in1(n2_bit_trigger_1_q[1]), .in2(or_2_out), .in3(not_3_out), .out(DoJmp),
    .sel(Op[1:0]));
  not not_3 (not_3_out, n2_bit_trigger_1_q[0]);
  not not_4 (not_4_out, SvEnd);
  IRCDecoder ircdecoder_1 (.IRC(IRC), .IHAddr(ircdecoder_1_ihaddr));
  nor nor_1 (Write, clk, SVSel, Jump);
  PC pc_1 (
    .Clock(clk), .B(out_14), .A(out_13), .command(PCop), .ClkWait(not_4_out), .SvAddr(SvAddrs),
    .JA({out_2, out_5}), .IRQ(IRQ), .rCnt(out_15), .IHAddr(ircdecoder_1_ihaddr), .IRQDone(IRQDone),
    .DoJump(DoJmp), ._0(_0));  // open: _111, _010101

  // Other names for the same wires on the sheet: A[3:0] = out_11; A_in[3:0] = out_13; B[3:0] = out_12;
  //   B_in[3:0] = out_14; data[3:0] = out_3; ID[3:0] = out_6; JmpA[7:0] = {out_2, out_5}; r5[3:0] = out_5;
  //   r4[3:0] = out_2; Output[7:0] = {out_4, out_7}; r2[3:0] = out_7; r1[3:0] = out_4; r0[3:0] = out_1;
  //   r3[3:0] = out_9; r6[3:0] = out_8; r7[3:0] = out_10; rCnt[7:0] = out_15

  // Notes on the sheet:
  //   register r7 contains pushed value
endmodule

module _2_bit_Trigger (
  input  Clock,
  input  [1:0] D,
  output [1:0] Q
);

  D_Flip_Flop d_ff_1 (.clk(Clock), .D(D[0]), .Q(Q[1]), .en(1'b1));  // open: Qn, preset, reset
  D_Flip_Flop d_ff_2 (.clk(Clock), .D(D[1]), .Q(Q[0]), .en(1'b1));  // open: Qn, preset, reset
endmodule

module Decode_Logic (
  input  Bit,
  input  [3:0] Op,
  output Digit,
  output Jump,
  output AluLogic,
  output Alu,
  output AluCarry,
  output FWright,
  output Address,
  output [3:0] AluOp,
  output SVR_Command,
  output SVR_Select,
  output rClkMv
);

  wire demultiplexer_1_out1, demultiplexer_1_out2, demultiplexer_1_out3, demultiplexer_1_out9;

  Demultiplexer #(.select(4), .enable("false")) demultiplexer_1 (
    .out1(demultiplexer_1_out1), .out2(demultiplexer_1_out2), .out3(demultiplexer_1_out3), .out4(AluLogic),
    .out5(SVR_Select), .out6(AluCarry), .out7(rClkMv), .out8(SVR_Command), .out9(demultiplexer_1_out9),
    .in(Bit), .sel(Op));  // open: out0, out10, out11, out12, out13, out14, out15
  and and_1 (Jump, Op[2], Op[3]);
  or or_1 (Digit, demultiplexer_1_out2, demultiplexer_1_out1);
  or or_2 (Address, demultiplexer_1_out2, demultiplexer_1_out3);
  Pull_Resistor pull_resistor_1 (.node(SVR_Select));
  Pull_Resistor pull_resistor_2 (.node(SVR_Command));
  or or_3 (Alu, AluLogic, AluCarry, demultiplexer_1_out9);

  assign AluOp = Op;
  assign FWright = AluCarry;

  // Other names for the same wires on the sheet: adress = Address; FlagWright = AluCarry; SVCmd = SVR_Command;
  //   SVSel = SVR_Select
endmodule

module PC (
  input  [7:0] JA,
  input  IRQ,
  input  [7:0] SvAddr,
  input  Clock,
  input  [7:0] IHAddr,
  input  DoJump,
  input  ClkWait,
  output [7:0] _111,
  output [7:0] rCnt,
  output [7:0] _010101,
  output IRQDone,
  output [3:0] B,
  output [3:0] A,
  output [3:0] command,
  output _0
);

  wire AddSel, and_1_out, buffer_1_out, buffer_2_out, buffer_3_out, ClkUpd, IRQDUpd, nor_1_out, not_1_out,
       not_2_out, not_3_out, or_1_out;
  wire [7:0] controlled_buffer_2_out, counter_1_q;

  Pull_Resistor #(.pull(1)) pull_resistor_1 (.node(IRQDUpd));
  assign IRQDUpd = IRQ ? ClkUpd : 1'bz;  // Controlled_Buffer controlled_buffer_1
  and and_1 (and_1_out, IRQ, ClkUpd);
  nor nor_1 (nor_1_out, IRQ, AddSel);
  T_Flip_Flop t_ff_1 (.clk(IRQDUpd), .T(1'b1), .Q(IRQDone), .reset(not_1_out), .en(1'b1));  // open: Qn, preset
  not not_1 (not_1_out, Clock);
  or or_1 (or_1_out, AddSel, and_1_out);
  Button button_1 (.out(_0));
  Counter #(.ongoal("stay")) counter_1 (
    .load(or_1_out), .D(_111), .count(nor_1_out), .Q(counter_1_q), .clk(buffer_1_out));  // open: carry, clr
  buf buffer_1 (buffer_1_out, buffer_2_out);
  buf buffer_2 (buffer_2_out, buffer_3_out);
  buf buffer_3 (buffer_3_out, ClkUpd);
  Register register_1 (.D(counter_1_q), .en(1'b1), .Q(rCnt), .clk(not_2_out));  // open: clr
  not not_2 (not_2_out, IRQDUpd);
  assign controlled_buffer_2_out = not_3_out ? counter_1_q : 8'bz;  // Controlled_Buffer controlled_buffer_2
  not not_3 (not_3_out, ClkWait);
  and and_2 (ClkUpd, not_3_out, Clock);
  assign controlled_buffer_2_out = ClkWait ? SvAddr : 8'bz;  // Controlled_Buffer controlled_buffer_3
  Multiplexer #(.width(8), .enable("false")) multiplexer_1 (.in0(IHAddr), .in1(JA), .out(_111), .sel(AddSel));
  ROM #(.dataWidth(12)) rom_1 (.addr(controlled_buffer_2_out), .data({command, A, B}), .sel(1'b1));
  and and_3 (AddSel, command[3], command[2], DoJump);

  assign _010101 = _111;

  // Other names for the same wires on the sheet: Clk = Clock; CntReg[7:0] = rCnt; DoJmp = DoJump; IHA[7:0] = IHAddr;
  //   SvA[7:0] = SvAddr; curAddr[7:0] = _111; toAddr[7:0] = _111

  // Notes on the sheet:
  //   IRQ writes to CNT on front (0->1)
  //   remmembers last address it was. => jump on this+1
  //   contents of rom_1 (hex, n*v repeats v):
  //   0 128 11c 110 125 11c 110 12c 11c 110 12c 11c 110 12f 11c 110 120 11a 110 127 11d 110 12f 11c 110
  //   122 11d 110 12c 11c 110 124 11c 110 121 11a 110 677 120 11a 110 140 151 150 140 600 c00 49*0 161 976
  //   750 741 600 c00 36*0 207 161 906 161 606 370
endmodule

module severalizer (
  input  [7:0] SvBeg,
  input  Clk,
  input  [7:0] SvLen,
  output [7:0] CmdAddrs,
  output End
);

  wire comparator_1_eq, shift_register_1_out;
  wire [7:0] Cnt;

  Comparator comparator_1 (.a(SvLen), .b(Cnt), .eq(comparator_1_eq));  // open: gt, lt
  Counter counter_1 (.count(1'b1), .Q(Cnt), .clk(Clk), .clr(shift_register_1_out));  // open: load, D, carry
  Shift_Register #(.length(1), .parallel("false")) shift_register_1 (
    .shift(1'b1), .in(comparator_1_eq), .clk(Clk), .out(shift_register_1_out));  // open: load, clr, d0, q0
  Comparator comparator_2 (.a(Cnt), .b({8{1'b0}}), .eq(End));  // open: gt, lt
  Adder adder_1 (.a(SvBeg), .b(Cnt), .out(CmdAddrs));  // open: cin, cout

  // Other names for the same wires on the sheet: Addrs[7:0] = CmdAddrs
endmodule

module SVDecoder (
  input  [3:0] B,
  input  Clk,
  output [7:0] SVBeg,
  output [7:0] SVLen
);

  wire [7:0] multiplexer_1_out, multiplexer_2_out;

  Multiplexer #(.select(4), .width(8), .enable("false")) multiplexer_1 (
    .in0(8'h89), .in1(8'h8c), .out(multiplexer_1_out), .sel(B));  // open: in2, in3, in4, in5, in6, in7, in8, in9, in10, in11, in12, in13, in14, in15
  Multiplexer #(.select(4), .width(8), .enable("false")) multiplexer_2 (
    .in0(8'h3), .in1(8'h3), .out(multiplexer_2_out), .sel(B));  // open: in2, in3, in4, in5, in6, in7, in8, in9, in10, in11, in12, in13, in14, in15
  Register register_1 (.D(multiplexer_1_out), .en(1'b1), .Q(SVBeg), .clk(Clk));  // open: clr
  Register register_2 (.D(multiplexer_2_out), .en(1'b1), .Q(SVLen), .clk(Clk));  // open: clr
endmodule

module IRCDecoder (
  input  [3:0] IRC,
  output [7:0] IHAddr
);

  Multiplexer #(.select(4), .width(8), .enable("false")) multiplexer_1 (
    .in0(8'h60), .in1(8'h65), .out(IHAddr), .sel(IRC));  // open: in2, in3, in4, in5, in6, in7, in8, in9, in10, in11, in12, in13, in14, in15

  // Other names for the same wires on the sheet: Code[3:0] = IRC
endmodule

module BinKeyboard (
  input  Key0,
  input  Rec,
  input  Key1,
  output [3:0] IRC,
  output IRQ
);

  wire controlled_buffer_1_out, controlled_buffer_2_out, d_ff_1_qn, d_ff_2_qn;
  wire [1:0] d_ff_1_q;

  assign controlled_buffer_1_out = d_ff_1_qn ? Key0 : 1'bz;  // Controlled_Buffer controlled_buffer_1
  assign controlled_buffer_2_out = d_ff_2_qn ? Key1 : 1'bz;  // Controlled_Buffer controlled_buffer_2
  D_Flip_Flop #(.trigger("high")) d_ff_1 (
    .clk(Key0), .D(controlled_buffer_1_out), .Q(d_ff_1_q[0]), .Qn(d_ff_1_qn), .en(1'b1), .reset(Rec));  // open: preset
  D_Flip_Flop #(.trigger("high")) d_ff_2 (
    .clk(Key1), .D(controlled_buffer_2_out), .Q(d_ff_1_q[1]), .Qn(d_ff_2_qn), .en(1'b1), .reset(Rec));  // open: preset
  or or_1 (IRQ, d_ff_1_q[0], d_ff_1_q[1]);
  Multiplexer #(.select(2), .width(4), .enable("false")) multiplexer_1 (
    .in1(4'b0000), .in2(4'b0001), .out(IRC), .sel(d_ff_1_q));  // open: in0, in3
endmodule
