// Logisim project Proccessor.circ as structural Verilog: 11 circuits, main circuit main
module MyALU (
  input  [3:0] Op,
  input  [3:0] B,
  input  [3:0] A,
  input  M,
  input  CIN,
  output A_B_bdc56332,
  output Sign,
  output [3:0] AluOut
);

  wire ALU_1_g, ALU_1_y1, ALU_1_y2, ALU_1_y3, ALU_1_y4, not_1_out, not_2_out, not_3_out, not_4_out,
       not_5_out, not_6_out, not_7_out, not_8_out, not_13_out;

  not not_1 (not_1_out, B[0]);
  not not_2 (not_2_out, B[3]);
  not not_3 (not_3_out, B[2]);
  not not_4 (not_4_out, B[1]);
  not not_5 (not_5_out, A[3]);
  not not_6 (not_6_out, A[2]);
  not not_7 (not_7_out, A[1]);
  not not_8 (not_8_out, A[0]);
  ALU ALU_1 (
    .S1(Op[0]), .S2(Op[1]), .S3(Op[2]), .S4(Op[3]), .B4(not_2_out), .A4(not_5_out), .B3(not_3_out),
    .A3(not_6_out), .B2(not_4_out), .A2(not_7_out), .B1(not_1_out), .A1(not_8_out), .M(M), .CIN(CIN),
    .G(ALU_1_g), .Y4(ALU_1_y4), .Y3(ALU_1_y3), .EQ(A_B_bdc56332), .Y2(ALU_1_y2), .Y1(ALU_1_y1));  // open: COUT, P
  not not_9 (AluOut[3], ALU_1_y4);
  not not_10 (AluOut[2], ALU_1_y3);
  not not_11 (AluOut[1], ALU_1_y2);
  not not_12 (AluOut[0], ALU_1_y1);
  not not_13 (not_13_out, A_B_bdc56332);
  and and_1 (Sign, not_13_out, ALU_1_g);
endmodule

module MyTrigger (
  input  [3:0] InputData,
  input  Clock,
  output [3:0] OutData
);

  Register #(.width(4)) register_1 (.D(InputData), .en(1'b1), .clk(Clock), .Q(OutData));  // open: clr
endmodule

module Registers (
  input  w,
  input  [3:0] data,
  input  [3:0] A,
  input  [3:0] B,
  input  [3:0] to,
  output [3:0] Output_bus_1,
  output [3:0] r0,
  output [3:0] r1,
  output [3:0] r2,
  output [3:0] Output_bus_2,
  output [3:0] r3,
  output [3:0] Output_bus_3,
  output [3:0] Output_bus_4,
  output [3:0] Output_bus_5,
  output [3:0] r4
);

  wire r0_w, r1_w, r2_w, r3_w, r4_w, r5_w, r6_w, r7_w;

  Demultiplexer #(.select(3), .enable("false")) demultiplexer_1 (
    .out0(r0_w), .out1(r1_w), .out2(r2_w), .out3(r3_w), .out4(r4_w), .out5(r5_w), .out6(r6_w), .out7(r7_w),
    .in(w), .sel(to[2:0]));
  MyTrigger MyTrigger_1 (.InputData(data), .OutData(r0), .Clock(r0_w));
  MyTrigger MyTrigger_2 (.InputData(data), .OutData(r1), .Clock(r1_w));
  MyTrigger MyTrigger_3 (.InputData(data), .OutData(r2), .Clock(r2_w));
  MyTrigger MyTrigger_4 (.InputData(data), .OutData(r3), .Clock(r3_w));
  MyTrigger MyTrigger_5 (.InputData(data), .OutData(Output_bus_3), .Clock(r4_w));
  MyTrigger MyTrigger_6 (.InputData(data), .OutData(Output_bus_4), .Clock(r5_w));
  MyTrigger MyTrigger_7 (.InputData(data), .OutData(Output_bus_5), .Clock(r6_w));
  MyTrigger MyTrigger_8 (.InputData(data), .OutData(r4), .Clock(r7_w));
  Multiplexer #(.select(3), .width(4), .enable("false")) multiplexer_1 (
    .in0(r0), .in1(r1), .in2(r2), .in3(r3), .in4(Output_bus_3), .in5(Output_bus_4), .in6(Output_bus_5),
    .in7(r4), .out(Output_bus_1), .sel(A[2:0]));
  Multiplexer #(.select(3), .width(4), .enable("false")) multiplexer_2 (
    .in0(r0), .in1(r1), .in2(r2), .in3(r3), .in4(Output_bus_3), .in5(Output_bus_4), .in6(Output_bus_5),
    .in7(r4), .out(Output_bus_2), .sel(B[2:0]));

  // Other names for the same wires on the sheet: r4_t[3:0] = Output_bus_3; r5[3:0] = Output_bus_4;
  //   r6[3:0] = Output_bus_5; r7[3:0] = r4
endmodule

module main (
  input  Input_1,
  output [3:0] r0,
  output [3:0] r4,
  output [3:0] r1,
  output [3:0] r5,
  output [3:0] r2,
  output [3:0] r6,
  output [3:0] r3,
  output [3:0] r7,
  output [3:0] OP
);

  wire address, Alu, and_1_out, and_2_out, cin, D, demultiplexer_1_out1, DoJmp, f, Jump, M, not_1_out,
       not_2_out, or_1_out, w, Write;
  wire [1:0] FF_output_bus_1, MyALU_1_sign;
  wire [3:0] A, A_in, AluOut, B, B_in, data, ID, multiplexer_1_out, PrCount_command, r0_t, r1_t, r2_t, r3_t,
       r4_t, r5_t, r6_t, r7_t, RD;

  Multiplexer #(.width(4), .enable("false")) multiplexer_1 (.in0(B), .in1(A), .out(multiplexer_1_out), .sel(D));
  Demultiplexer #(.enable("false")) demultiplexer_1 (
    .out0(w), .out1(demultiplexer_1_out1), .in(Write), .sel(and_1_out));
  and and_1 (and_1_out, address, D);
  Multiplexer #(.select(2), .width(4), .enable("false")) multiplexer_2 (
    .in0(B), .in1(B_in), .in2(RD), .in3(B), .out(ID), .sel({address, D}));
  MyRam RAM_CPU (
    .Input_bus_1(data), .Output_bus_1(RD), .Input_bus_2(multiplexer_1_out), .w(demultiplexer_1_out1),
    .Output_bus_2(r0), .Output_bus_3(r1), .Output_bus_4(r2), .Output_bus_5(r3), .Output_bus_6(r4),
    .Output_bus_7(r5), .Output_bus_8(r6), .Output_bus_9(r7));
  Multiplexer #(.width(4), .enable("false")) multiplexer_3 (.in0(ID), .in1(AluOut), .out(data), .sel(Alu));
  MyALU MyALU_1 (
    .Op(OP), .A_B_bdc56332(MyALU_1_sign[1]), .Sign(MyALU_1_sign[0]), .AluOut(AluOut), .B(ID), .A(A), .M(M),
    .CIN(cin));
  Registers RegFile (
    .A(A_in), .B(B_in), .r0(r0_t), .r1(r1_t), .r2(r2_t), .r3(r3_t), .data(data), .w(w), .to(A_in),
    .Output_bus_3(r4_t), .Output_bus_2(B), .Output_bus_1(A), .Output_bus_4(r5_t), .Output_bus_5(r6_t),
    .r4(r7_t));
  L_2_bit_Trigger_61c2be1b FF (.Input_bus_1(MyALU_1_sign), .Output_bus_1(FF_output_bus_1), .Input_1(and_2_out));
  and and_2 (and_2_out, f, not_1_out);
  not not_1 (not_1_out, Input_1);
  or or_1 (or_1_out, FF_output_bus_1[0], FF_output_bus_1[1]);
  not not_2 (not_2_out, FF_output_bus_1[1]);
  PC PrCount (.Clock(Input_1), .B(B_in), .A(A_in), .command(PrCount_command), .DoJump(DoJmp));
  Multiplexer #(.select(2), .enable("false")) multiplexer_4 (
    .in0(FF_output_bus_1[1]), .in1(FF_output_bus_1[0]), .in2(or_1_out), .in3(not_2_out), .out(DoJmp),
    .sel(OP[1:0]));
  Decode_Logic_0a78f3ad Decode_Logic (
    .Jump(Jump), .AluLogic(M), .Alu(Alu), .Bit(1'b1), .AluCarry(cin), .FWright(f), .Address(address),
    .AluOp(OP), .Op(PrCount_command), .Digit(D));
  nor nor_1 (Write, Input_1, Jump);

  // Other names for the same wires on the sheet: ram0[3:0] = r0; ram1[3:0] = r1; ram2[3:0] = r2; ram3[3:0] = r3;
  //   ram4[3:0] = r4; ram5[3:0] = r5; ram6[3:0] = r6; ram7[3:0] = r7
endmodule

module L_2_bit_Trigger_61c2be1b (
  input  [1:0] Input_bus_1,
  input  Input_1,
  output [1:0] Output_bus_1
);

  Register #(.width(2)) register_1 (.D(Input_bus_1), .en(1'b1), .clk(Input_1), .Q(Output_bus_1));  // open: clr
endmodule

module Decode_Logic_0a78f3ad (
  input  Bit,
  input  [3:0] Op,
  output Digit,
  output Jump,
  output AluLogic,
  output Alu,
  output AluCarry,
  output FWright,
  output Address,
  output [3:0] AluOp
);

  wire demultiplexer_1_out1, demultiplexer_1_out2, demultiplexer_1_out3, demultiplexer_1_out9;

  Demultiplexer #(.select(4), .enable("false")) demultiplexer_1 (
    .out1(demultiplexer_1_out1), .out2(demultiplexer_1_out2), .out3(demultiplexer_1_out3), .out4(AluLogic),
    .out6(AluCarry), .out9(demultiplexer_1_out9), .in(Bit), .sel(Op));  // open: out0, out5, out7, out8, out10, out11, out12, out13, out14, out15
  and and_1 (Jump, Op[2], Op[3]);
  or or_1 (Digit, demultiplexer_1_out2, demultiplexer_1_out1);
  or or_2 (Address, demultiplexer_1_out2, demultiplexer_1_out3);
  or or_3 (Alu, AluLogic, AluCarry, demultiplexer_1_out9);

  assign AluOp = Op;
  assign FWright = AluCarry;

  // Other names for the same wires on the sheet: adress = Address; FlagWright = AluCarry
endmodule

module PC (
  input  Clock,
  input  DoJump,
  output [3:0] B,
  output [3:0] A,
  output [3:0] command
);

  wire and_1_out, not_1_out;
  wire [7:0] counter_1_q;

  and and_1 (and_1_out, command[3], command[2], DoJump);
  not not_1 (not_1_out, and_1_out);
  Counter counter_1 (
    .load(and_1_out), .up(not_1_out), .count(not_1_out), .clk(Clock), .D({A, B}), .Q(counter_1_q));  // open: clr, carry
  ROM #(.dataWidth(12)) ROM_CPU_123wd (.addr(counter_1_q), .data({command, A, B}));

  // Other names for the same wires on the sheet: Address[7:0] = {A, B}

  // Notes on the sheet:
  //   contents of ROM_CPU_123wd (hex, n*v repeats v):
  //   0 121 100 116 201 113 902 201 902 110 201 114 902 201 115 902 201 112 902 201 111 902 201 137 101 60
  //   663 c30 340 10 612 d29 371 674 e29 51 952 361 256 666 c1e 61 962 264 902 677 c19
endmodule

module FPGA (
  input  [3:0] in_1,
  input  [3:0] in_2,
  input  [3:0] in_3,
  input  [3:0] in_4,
  input  in_5,
  input  in_6,
  input  in_7,
  output [3:0] out_8
);

  wire [3:0] multiplexer_1_out, RD;

  Multiplexer #(.width(4), .enable("false")) multiplexer_1 (
    .in0(in_3), .in1(in_4), .out(multiplexer_1_out), .sel(in_5));
  Multiplexer #(.select(2), .width(4), .enable("false")) multiplexer_2 (
    .in0(in_3), .in1(in_2), .in2(RD), .in3(in_3), .out(out_8), .sel({in_6, in_5}));
  RAM #(.addrWidth(4), .dataWidth(4)) ram_1 (
    .addr(multiplexer_1_out), .data(RD), .clk(in_7), .ld(1'b1));  // open: sel, clr

  // Other names for the same wires on the sheet: D = in_5; address = in_6; A[3:0] = in_4; B[3:0] = in_3;
  //   B_in[3:0] = in_2; data[3:0] = in_1; ID[3:0] = out_8; write = in_7
endmodule

module example (
);

  RAM #(.addrWidth(4), .dataWidth(4), .databus("bibus")) dcwefwf ();  // open: addr, we, oe, clk, din, dout
endmodule

module ALU (
  input  S1,
  input  S2,
  input  S3,
  input  S4,
  input  B4,
  input  A4,
  input  B3,
  input  A3,
  input  B2,
  input  A2,
  input  B1,
  input  A1,
  input  M,
  input  CIN,
  output G,
  output COUT,
  output P,
  output Y4,
  output Y3,
  output EQ,
  output Y2,
  output Y1
);

  wire and_1_out, and_2_out, and_3_out, and_4_out, and_5_out, and_6_out, and_7_out, and_8_out, and_9_out,
       and_10_out, and_11_out, and_12_out, and_13_out, and_14_out, and_15_out, and_16_out, and_17_out,
       and_18_out, and_19_out, and_20_out, and_21_out, and_22_out, and_23_out, and_24_out, and_25_out,
       and_26_out, and_27_out, and_28_out, buffer_1_out, buffer_2_out, buffer_3_out, buffer_4_out,
       nand_1_out, nand_3_out, nor_1_out, nor_2_out, nor_3_out, nor_4_out, nor_5_out, nor_6_out, nor_7_out,
       nor_8_out, nor_10_out, nor_11_out, nor_12_out, not_1_out, not_2_out, not_3_out, not_4_out, not_5_out,
       xor_1_out, xor_2_out, xor_3_out, xor_4_out;

  not not_1 (not_1_out, B4);
  not not_2 (not_2_out, B3);
  not not_3 (not_3_out, B2);
  not not_4 (not_4_out, B1);
  not not_5 (not_5_out, M);
  and and_1 (and_1_out, B4, S1, A4);
  and and_2 (and_2_out, A4, S2, not_1_out);
  and and_3 (and_3_out, not_1_out, S3);
  and and_4 (and_4_out, S4, B4);
  buf buffer_1 (buffer_1_out, A4);
  and and_5 (and_5_out, B3, S1, A3);
  and and_6 (and_6_out, A3, S2, not_2_out);
  and and_7 (and_7_out, not_2_out, S3);
  and and_8 (and_8_out, S4, B3);
  buf buffer_2 (buffer_2_out, A3);
  and and_9 (and_9_out, B2, S1, A2);
  and and_10 (and_10_out, A2, S2, not_3_out);
  and and_11 (and_11_out, not_3_out, S3);
  and and_12 (and_12_out, S4, B2);
  buf buffer_3 (buffer_3_out, A2);
  and and_13 (and_13_out, B1, S1, A1);
  and and_14 (and_14_out, A1, S2, not_4_out);
  and and_15 (and_15_out, not_4_out, S3);
  and and_16 (and_16_out, S4, B1);
  buf buffer_4 (buffer_4_out, A1);
  nor nor_1 (nor_1_out, and_1_out, and_2_out);
  nor nor_2 (nor_2_out, and_3_out, and_4_out, buffer_1_out);
  nor nor_3 (nor_3_out, and_5_out, and_6_out);
  nor nor_4 (nor_4_out, and_7_out, and_8_out, buffer_2_out);
  nor nor_5 (nor_5_out, and_9_out, and_10_out);
  nor nor_6 (nor_6_out, and_11_out, and_12_out, buffer_3_out);
  nor nor_7 (nor_7_out, and_13_out, and_14_out);
  nor nor_8 (nor_8_out, and_15_out, and_16_out, buffer_4_out);
  xor xor_1 (xor_1_out, nor_1_out, nor_2_out);
  xor xor_2 (xor_2_out, nor_3_out, nor_4_out);
  xor xor_3 (xor_3_out, nor_5_out, nor_6_out);
  xor xor_4 (xor_4_out, nor_7_out, nor_8_out);
  and and_17 (and_17_out, nor_1_out, nor_4_out);
  and and_18 (and_18_out, nor_1_out, nor_3_out, nor_6_out);
  and and_19 (and_19_out, nor_1_out, nor_3_out, nor_5_out, nor_8_out);
  nand nand_1 (nand_1_out, nor_1_out, nor_3_out, nor_5_out, nor_7_out, CIN);
  nand nand_2 (P, nor_1_out, nor_3_out, nor_5_out, nor_7_out);
  and and_20 (and_20_out, CIN, nor_7_out, nor_5_out, nor_3_out, not_5_out);
  and and_21 (and_21_out, nor_5_out, nor_3_out, nor_8_out, not_5_out);
  and and_22 (and_22_out, nor_3_out, nor_6_out, not_5_out);
  and and_23 (and_23_out, nor_4_out, not_5_out);
  and and_24 (and_24_out, CIN, nor_7_out, nor_5_out, not_5_out);
  and and_25 (and_25_out, nor_5_out, nor_8_out, not_5_out);
  and and_26 (and_26_out, nor_6_out, not_5_out);
  and and_27 (and_27_out, CIN, nor_7_out, not_5_out);
  and and_28 (and_28_out, nor_8_out, not_5_out);
  nand nand_3 (nand_3_out, CIN, not_5_out);
  nor nor_9 (G, nor_2_out, and_17_out, and_18_out, and_19_out);
  nor nor_10 (nor_10_out, and_20_out, and_21_out, and_22_out, and_23_out);
  nor nor_11 (nor_11_out, and_24_out, and_25_out, and_26_out);
  nor nor_12 (nor_12_out, and_27_out, and_28_out);
  nor nor_13 (COUT, G, nand_1_out);
  xor xor_5 (Y4, xor_1_out, nor_10_out);
  xor xor_6 (Y3, xor_2_out, nor_11_out);
  xor xor_7 (Y2, xor_3_out, nor_12_out);
  xor xor_8 (Y1, xor_4_out, nand_3_out);
  and and_29 (EQ, Y3, Y4, Y1, Y2);
endmodule

module MyRam (
  input  [3:0] Input_bus_1,
  input  [3:0] Input_bus_2,
  input  w,
  output [3:0] Output_bus_1,
  output [3:0] Output_bus_2,
  output [3:0] Output_bus_3,
  output [3:0] Output_bus_4,
  output [3:0] Output_bus_5,
  output [3:0] Output_bus_6,
  output [3:0] Output_bus_7,
  output [3:0] Output_bus_8,
  output [3:0] Output_bus_9
);

  wire r0_w, r1_w, r2_w, r3_w, r4_w, r5_w, r6_w, r7_w, r8_w, r9_w, r10_w, r11_w, r12_w, r13_w, r14_w, r15_w;
  wire [3:0] r8, r9, r10, r11, r12, r13, r14, r15;

  Demultiplexer #(.select(4), .enable("false")) demultiplexer_1 (
    .out0(r0_w), .out1(r1_w), .out2(r2_w), .out3(r3_w), .out4(r4_w), .out5(r5_w), .out6(r6_w), .out7(r7_w),
    .out8(r8_w), .out9(r9_w), .out10(r10_w), .out11(r11_w), .out12(r12_w), .out13(r13_w), .out14(r14_w),
    .out15(r15_w), .in(w), .sel(Input_bus_2));
  MyTrigger MyTrigger_1 (.InputData(Input_bus_1), .OutData(Output_bus_2), .Clock(r0_w));
  MyTrigger MyTrigger_2 (.InputData(Input_bus_1), .OutData(Output_bus_3), .Clock(r1_w));
  MyTrigger MyTrigger_3 (.InputData(Input_bus_1), .OutData(Output_bus_4), .Clock(r2_w));
  MyTrigger MyTrigger_4 (.InputData(Input_bus_1), .OutData(Output_bus_5), .Clock(r3_w));
  MyTrigger MyTrigger_5 (.InputData(Input_bus_1), .OutData(Output_bus_6), .Clock(r4_w));
  MyTrigger MyTrigger_6 (.InputData(Input_bus_1), .OutData(Output_bus_7), .Clock(r5_w));
  MyTrigger MyTrigger_7 (.InputData(Input_bus_1), .OutData(Output_bus_8), .Clock(r6_w));
  MyTrigger MyTrigger_8 (.InputData(Input_bus_1), .OutData(Output_bus_9), .Clock(r7_w));
  MyTrigger MyTrigger_9 (.InputData(Input_bus_1), .OutData(r8), .Clock(r8_w));
  MyTrigger MyTrigger_10 (.InputData(Input_bus_1), .OutData(r9), .Clock(r9_w));
  MyTrigger MyTrigger_11 (.InputData(Input_bus_1), .OutData(r10), .Clock(r10_w));
  MyTrigger MyTrigger_12 (.InputData(Input_bus_1), .OutData(r11), .Clock(r11_w));
  MyTrigger MyTrigger_13 (.InputData(Input_bus_1), .OutData(r12), .Clock(r12_w));
  MyTrigger MyTrigger_14 (.InputData(Input_bus_1), .OutData(r13), .Clock(r13_w));
  MyTrigger MyTrigger_15 (.InputData(Input_bus_1), .OutData(r14), .Clock(r14_w));
  MyTrigger MyTrigger_16 (.InputData(Input_bus_1), .OutData(r15), .Clock(r15_w));
  Multiplexer #(.select(4), .width(4), .enable("false")) multiplexer_1 (
    .in0(Output_bus_2), .in1(Output_bus_3), .in2(Output_bus_4), .in3(Output_bus_5), .in4(Output_bus_6),
    .in5(Output_bus_7), .in6(Output_bus_8), .in7(Output_bus_9), .in8(r8), .in9(r9), .in10(r10), .in11(r11),
    .in12(r12), .in13(r13), .in14(r14), .in15(r15), .out(Output_bus_1), .sel(Input_bus_2));

  // Other names for the same wires on the sheet: data[3:0] = Input_bus_1; r0[3:0] = Output_bus_2;
  //   r1[3:0] = Output_bus_3; r2[3:0] = Output_bus_4; r3[3:0] = Output_bus_5; r4[3:0] = Output_bus_6;
  //   r5[3:0] = Output_bus_7; r6[3:0] = Output_bus_8; r7[3:0] = Output_bus_9; to[3:0] = Input_bus_2
endmodule
